// Logisim project half_adder.circ as structural Verilog: 1 circuit, main circuit main
module main (
  input  A,
  input  B,
  output out_3,
  output out_4
);

  wire and_1_out, and_3_out, not_1_out, not_2_out;

  not not_1 (not_1_out, A);
  not not_2 (not_2_out, B);
  and and_1 (and_1_out, not_2_out, A);
  and and_2 (out_4, B, A);
  and and_3 (and_3_out, B, not_1_out);
  or or_1 (out_3, and_3_out, and_1_out);

  // Notes on the sheet:
  //   s=!ab+a!b
endmodule
